// Logisim project lab07_base.circ as structural Verilog: 4 circuits, main circuit main
module register_file (
  input  [7:0] data_write,
  input  clear,
  input  clk,
  input  write_enable,
  input  [1:0] write_reg,
  input  [1:0] read_reg,
  input  reset,
  output [7:0] data_read
);

  wire demultiplexer_1_out0, demultiplexer_1_out1, demultiplexer_1_out2, demultiplexer_1_out3;
  wire [7:0] demultiplexer_2_out0, demultiplexer_2_out1, demultiplexer_2_out2, demultiplexer_2_out3,
       multiplexer_1_out, REG_00_q, REG_01_q, REG_3_q, REG_4_q;

  Multiplexer #(.width(8)) multiplexer_1 (.in0(data_write), .in1({8{1'b0}}), .out(multiplexer_1_out), .sel(clear));
  Demultiplexer #(.select(2)) demultiplexer_1 (
    .out0(demultiplexer_1_out0), .out1(demultiplexer_1_out1), .out2(demultiplexer_1_out2),
    .out3(demultiplexer_1_out3), .in(write_enable), .sel(write_reg));
  Demultiplexer #(.select(2), .width(8)) demultiplexer_2 (
    .out0(demultiplexer_2_out0), .out1(demultiplexer_2_out1), .out2(demultiplexer_2_out2),
    .out3(demultiplexer_2_out3), .in(multiplexer_1_out), .sel(write_reg));
  Register REG_00 (.D(demultiplexer_2_out0), .en(demultiplexer_1_out0), .clk(clk), .Q(REG_00_q), .clr(reset));
  Register REG_01 (.D(demultiplexer_2_out1), .en(demultiplexer_1_out1), .clk(clk), .Q(REG_01_q), .clr(reset));
  Register REG_3 (.D(demultiplexer_2_out2), .en(demultiplexer_1_out2), .clk(clk), .Q(REG_3_q), .clr(reset));
  Register REG_4 (.D(demultiplexer_2_out3), .en(demultiplexer_1_out3), .clk(clk), .Q(REG_4_q), .clr(reset));
  Multiplexer #(.select(2), .width(8)) multiplexer_2 (
    .in0(REG_00_q), .in1(REG_01_q), .in2(REG_3_q), .in3(REG_4_q), .out(data_read), .sel(read_reg));

  // Notes on the sheet:
  //   clear_write
endmodule

module alu (
  input  [7:0] A,
  input  [7:0] B,
  input  op,
  output [7:0] data_out
);

  wire [7:0] adder_1_out, multiplier_1_out;

  Adder adder_1 (.a(A), .b(B), .out(adder_1_out));  // open: cin, cout
  Multiplier multiplier_1 (.a(A), .b(B), .out(multiplier_1_out));  // open: cin, cout
  Multiplexer #(.width(8)) multiplexer_1 (.in0(adder_1_out), .in1(multiplier_1_out), .out(data_out), .sel(op));
endmodule

module instr_decoder (
  input  [7:0] instr,
  output [1:0] imm,
  output [1:0] read_reg,
  output [1:0] write_reg,
  output write_en,
  output alu_op,
  output reg_clear
);

  or or_1 (write_en, instr[6], instr[7]);
  not not_1 (alu_op, instr[6]);
  and and_1 (reg_clear, instr[6], instr[7]);

  assign imm = instr[1:0];
  assign read_reg = instr[3:2];
  assign write_reg = instr[5:4];
endmodule

module main (
  input  [7:0] in_1
);

  wire clk_out, instr_decoder_1_alu_op, instr_decoder_1_reg_clear, instr_decoder_1_write_en, reset_out;
  wire [1:0] instr_decoder_1_imm, instr_decoder_1_read_reg, instr_decoder_1_write_reg;
  wire [7:0] alu_1_data_out, bit_extender_1_out, register_file_1_data_read;

  Button clk (.out(clk_out));
  Button reset (.out(reset_out));
  instr_decoder instr_decoder_1 (
    .instr(in_1), .imm(instr_decoder_1_imm), .read_reg(instr_decoder_1_read_reg),
    .write_reg(instr_decoder_1_write_reg), .write_en(instr_decoder_1_write_en),
    .alu_op(instr_decoder_1_alu_op), .reg_clear(instr_decoder_1_reg_clear));
  assign bit_extender_1_out = {{6{1'b0}}, instr_decoder_1_imm};  // Bit_Extender bit_extender_1
  register_file register_file_1 (
    .data_write(alu_1_data_out), .clear(instr_decoder_1_reg_clear), .clk(clk_out),
    .write_enable(instr_decoder_1_write_en), .write_reg(instr_decoder_1_write_reg),
    .read_reg(instr_decoder_1_read_reg), .reset(reset_out), .data_read(register_file_1_data_read));
  alu alu_1 (
    .A(register_file_1_data_read), .B(bit_extender_1_out), .op(instr_decoder_1_alu_op),
    .data_out(alu_1_data_out));
endmodule
